// Logisim project Q1.circ as structural Verilog: 1 circuit, main circuit main
module main (
  input  a,
  input  b,
  input  c,
  output x,
  output y
);

  wire and_1_out, and_2_out, xor_1_out;

  xor odd_parity_1 (x, a, b, c);
  and and_1 (and_1_out, a, b);
  xor xor_1 (xor_1_out, a, b);
  and and_2 (and_2_out, xor_1_out, c);
  or or_1 (y, and_1_out, and_2_out);
endmodule
