// Logisim project Q2.circ as structural Verilog: 1 circuit, main circuit main
module main (
  input  in_1,
  input  in_2,
  output out_3
);

  wire and_1_out, and_2_out, and_3_out, and_4_out, and_6_out, and_7_out, d_ff_1_q, j_k_ff_1_q, not_1_out,
       not_2_out, or_1_out, or_3_out, or_4_out;

  not not_1 (not_1_out, in_1);
  not not_2 (not_2_out, in_2);
  and and_1 (and_1_out, not_1_out, not_2_out);
  and and_2 (and_2_out, not_2_out, j_k_ff_1_q);
  and and_3 (and_3_out, j_k_ff_1_q, not_2_out);
  and and_4 (and_4_out, not_1_out, not_2_out);
  // AND_Gate and_5 has open pins: in1=not_2_out, in3=d_ff_1_q, out=open
  and and_6 (and_6_out, not_1_out, not_2_out);
  or or_1 (or_1_out, and_1_out, and_2_out);
  or or_2 (out_3, and_6_out, not_1_out);
  or or_3 (or_3_out, and_3_out, and_4_out);
  D_Flip_Flop d_ff_1 (.clk(or_1_out), .Q(d_ff_1_q));  // open: D, Qn, preset, en, reset
  and and_7 (and_7_out, j_k_ff_1_q, not_1_out);
  buf or_4 (or_4_out, and_7_out);  // OR_Gate
  J_K_Flip_Flop j_k_ff_1 (.J(or_3_out), .K(or_4_out), .Q(j_k_ff_1_q));  // open: clk, Qn, preset, en, reset
endmodule
