// Logisim project Q3.circ as structural Verilog: 1 circuit, main circuit main
module main (
);

  wire and_1_out, and_2_out, and_3_out, and_5_out, and_6_out, and_7_out, and_8_out, clock_1_out, j_k_ff_1_q,
       j_k_ff_2_q, j_k_ff_3_q, not_1_out, not_2_out, not_3_out, or_1_out, or_2_out, or_3_out, or_4_out;

  Clock clock_1 (.out(clock_1_out));
  J_K_Flip_Flop j_k_ff_1 (
    .J(and_5_out), .clk(clock_1_out), .K(clock_1_out), .Q(j_k_ff_1_q));  // open: Qn, preset, en, reset
  J_K_Flip_Flop j_k_ff_2 (
    .J(and_7_out), .clk(clock_1_out), .K(and_8_out), .Q(j_k_ff_2_q));  // open: Qn, preset, en, reset
  J_K_Flip_Flop j_k_ff_3 (
    .J(and_6_out), .clk(clock_1_out), .K(and_3_out), .Q(j_k_ff_3_q));  // open: Qn, preset, en, reset
  not not_1 (not_1_out, j_k_ff_1_q);
  not not_2 (not_2_out, j_k_ff_2_q);
  not not_3 (not_3_out, j_k_ff_3_q);
  and and_1 (and_1_out, not_1_out, not_2_out);
  and and_2 (and_2_out, j_k_ff_2_q, j_k_ff_1_q);
  and and_3 (and_3_out, j_k_ff_1_q, j_k_ff_3_q);
  or or_1 (or_1_out, j_k_ff_2_q, j_k_ff_3_q);
  and and_4 (clock_1_out, j_k_ff_1_q, or_1_out, or_1_out);
  or or_2 (or_2_out, j_k_ff_2_q, not_3_out);
  or or_3 (or_3_out, not_3_out, not_1_out);
  or or_4 (or_4_out, and_1_out, and_2_out);
  and and_5 (and_5_out, not_1_out, or_2_out);
  and and_6 (and_6_out, not_3_out, or_4_out);
  and and_7 (and_7_out, not_2_out, or_3_out);
  and and_8 (and_8_out, or_3_out, j_k_ff_2_q);
endmodule
